// Logisim project demo.circ as structural Verilog: 2 circuits, main circuit main
module main (
);

  Cool_Circuit_Bro Cool_Circuit_Bro ();  // open: Num_1, Num_2, Carry_out, Output
endmodule

module Cool_Circuit_Bro (
  input  [1:0] Num_1,
  input  [1:0] Num_2,
  output [1:0] Output,
  output Carry_out
);

  Adder #(.width(2)) adder_1 (.a(Num_1), .b(Num_2), .out(Output), .cout(Carry_out));  // open: cin
endmodule
