// Logisim project example.circ as structural Verilog: 1 circuit, main circuit main
module main (
  input  [3:0] in_1,
  input  [3:0] in_2,
  output [3:0] out_3,
  output out_4
);

  Multiplexer #(.width(4)) multiplexer_1 (.in0(in_1), .in1(in_2), .out(out_3), .sel(out_4));  // open: en
  Button Click_Me (.out(out_4));

  // Notes on the sheet:
  //   Multiplexer Example:
  //   Splitter Ex
  //   <- Look at the output!
endmodule
