// Logisim project 1bit_alu.circ as structural Verilog: 1 circuit, main circuit main
module main (
  input  A,
  input  B,
  input  [1:0] Opperation,
  input  Sub,
  output out_5,
  output out_6
);

  wire adder_1_out, and_1_out, Mux, not_1_out, or_1_out;

  Multiplexer multiplexer_1 (.in0(B), .in1(not_1_out), .out(Mux), .sel(Sub));  // open: en
  not not_1 (not_1_out, B);
  and and_1 (and_1_out, A, Mux);
  or or_1 (or_1_out, A, Mux);
  Adder #(.width(1)) adder_1 (.a(A), .b(Mux), .out(adder_1_out), .cout(out_6));  // open: cin
  Multiplexer #(.select(2)) multiplexer_2 (
    .in1(and_1_out), .in2(or_1_out), .in3(adder_1_out), .out(out_5), .sel(Opperation));  // open: in0, en

  // Other names for the same wires on the sheet: C_Out = out_6; isSub = Sub; Op[1:0] = Opperation; Res = out_5

  // Notes on the sheet:
  //   Very Basic 1-bit ALU
  //   Operations: 0 (N/a) 1 (AND) 2 (OR) 3 (Add)
endmodule
